# Fritzing sketch BatteryChargeRig_four_battery_module (saved by Fritzing 0.9.4)
perfboards: 1

parts:
  Bat3 = battery_holder_dual_18650 [part_number=TBH-18650-2A-P]
  Bat4 = battery_holder_dual_18650 [part_number=TBH-18650-2A-P]
  TP5 = TP4056 [chip_label=TP4056 package="DIP (Dual Inline) [THT]"]
  TP6 = TP4056 [chip_label=TP4056 package="DIP (Dual Inline) [THT]"]
  TP7 = TP4056 [chip_label=TP4056 package="DIP (Dual Inline) [THT]"]
  TP8 = TP4056 [chip_label=TP4056 package="DIP (Dual Inline) [THT]"]
  Part2 = Adafruit ADS1015 12Bit I2C ADC [part_number="Adafruit #1083"]

nets:
  N1: Bat3.+#0, TP7.pin5
  N2: Bat3.+#1, TP6.pin5
  N3: Bat3.+#2, TP6.pin4, Part2.AIN3
  N4: Bat3.+#3, TP7.pin4, Part2.AIN2
  N5: Bat4.+#0, TP8.pin5
  N6: Bat4.+#1, TP5.pin5
  N7: Bat4.+#2, TP5.pin4, Part2.AIN1
  N8: Bat4.+#3, TP8.pin4, Part2.AIN0
  N9: TP8.pin2, Part2.GND

custom parts:
  battery_holder_dual_18650: TBH-18650-2A-P dual 18650 battery holder.
  TP4056: A DIP stand-in part for whatever IC you want. With 6 pins on a 300mil dual inline package (DIP) footprint.
  Adafruit ADS1015 12Bit I2C ADC: For microcontrollers without an analog-to-digital converter or when you want a higher-precision ADC, the ADS1015 provides 12-bit precision at 3300 samples/second over I2C. The chip can be configured as 4 single-ended input channels, or two differential channels. As a nice bonus, it even includes a programmable gain amplifier, up to x16, to help boost up smaller single/differential signals to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
